// Digital circuit Deslocador_MAIN.dig as structural Verilog
module Deslocador_MAIN (
  input  [31:0] A,
  input  [31:0] B,
  output [31:0] S
);

  wire b0, b1, b2, b3, b4;
  wire [31:0] _4x_s, _8x_s, _16x_s, deslocador_32_left_1_s;
  wire [31:5] not_1_out;

  assign {not_1_out, b4, b3, b2, b1, b0} = ~B;  // Not not_1, 32 bits wide
  Deslocador_32_left deslocador_32_left_1 (.A(A), .sh(b0), .S(deslocador_32_left_1_s));
  Desloca_2x _4x (.A(deslocador_32_left_1_s), .sh(b1), .S(_4x_s));
  Desloca_4x _8x (.A(_4x_s), .sh(b2), .S(_8x_s));
  Desloca_8x _16x (.A(_8x_s), .sh(b3), .S(_16x_s));
  Desloca_16x _32x (.A(_16x_s), .sh(b4), .S(S));
endmodule
