// Digital circuit Deslocador_32bit_right.dig as structural Verilog
module Deslocador_32bit_right (
  input  [31:0] A,
  input  sh,
  output [31:0] S
);

  wire undriven;

  Deslocador_4bit_fim deslocador_4bit_fim_1 (.A(A[31:28]), .sh(sh), .in(undriven), .S(S[31:28]));
endmodule
