// Digital circuit Somador_32bit.dig as structural Verilog
module Somador_32bit (
  input  [31:0] A,
  input  [31:0] B,
  output [31:0] S
);

  wire carry_la_1_co, carry_la_2_co, carry_la_3_co, carry_la_4_co, carry_la_5_co, carry_la_6_co,
       carry_la_7_co;

  Carry_LA carry_la_1 (.Cin(1'b0), .A(A[3:0]), .B(B[3:0]), .S(S[3:0]), .Co(carry_la_1_co));
  Carry_LA carry_la_2 (.Cin(carry_la_1_co), .A(A[7:4]), .B(B[7:4]), .S(S[7:4]), .Co(carry_la_2_co));
  Carry_LA carry_la_3 (.Cin(carry_la_2_co), .A(A[11:8]), .B(B[11:8]), .S(S[11:8]), .Co(carry_la_3_co));
  Carry_LA carry_la_4 (.Cin(carry_la_3_co), .A(A[15:12]), .B(B[15:12]), .S(S[15:12]), .Co(carry_la_4_co));
  Carry_LA carry_la_5 (.Cin(carry_la_4_co), .A(A[19:16]), .B(B[19:16]), .S(S[19:16]), .Co(carry_la_5_co));
  Carry_LA carry_la_6 (.Cin(carry_la_5_co), .A(A[23:20]), .B(B[23:20]), .S(S[23:20]), .Co(carry_la_6_co));
  Carry_LA carry_la_7 (.Cin(carry_la_6_co), .A(A[27:24]), .B(B[27:24]), .S(S[27:24]), .Co(carry_la_7_co));
  Carry_LA carry_la_8 (.Cin(carry_la_7_co), .A(A[31:28]), .B(B[31:28]), .S(S[31:28]));  // open: Co
endmodule
