// Digital circuit Subtrator_32Bit.dig as structural Verilog
module Subtrator_32Bit (
  input  [31:0] A,
  input  [31:0] B,
  output [31:0] S
);

  wire [31:0] not_1_out, somador_32bit_1_s;

  assign not_1_out = ~B;  // Not not_1, 32 bits wide
  Somador_32bit somador_32bit_1 (.A(32'h1), .B(not_1_out), .S(somador_32bit_1_s));
  Somador_32bit somador_32bit_2 (.A(A), .B(somador_32bit_1_s), .S(S));
endmodule
