// Digital circuit ULA.dig as structural Verilog
module ULA (
  input  [31:0] A,
  input  [31:0] B,
  input  [2:0] fun,
  output [31:0] G,
  output [31:0] zero
);

  wire [31:0] and_1_out, deslocador_main_1_s, deslocador_right_main_1_s, not_1_out, or_1_out,
       somador_32bit_1_s, subtrator_32bit_1_s, xor_1_out;

  Somador_32bit somador_32bit_1 (.A(A), .B(B), .S(somador_32bit_1_s));
  Subtrator_32Bit subtrator_32bit_1 (.A(A), .B(B), .S(subtrator_32bit_1_s));
  assign and_1_out = A & B;  // And and_1, 32 bits wide
  assign or_1_out = A | B;  // Or or_1, 32 bits wide
  assign xor_1_out = A ^ B;  // XOr xor_1, 32 bits wide
  assign not_1_out = ~A;  // Not not_1, 32 bits wide
  Deslocador_MAIN deslocador_main_1 (.A(A), .B(B), .S(deslocador_main_1_s));
  Deslocador_right_main deslocador_right_main_1 (.A(A), .B(B), .S(deslocador_right_main_1_s));
  Multiplexer #(.Selector_Bits(3), .Bits(32)) multiplexer_1 (
    .sel(fun), .in_0(somador_32bit_1_s), .in_1(subtrator_32bit_1_s), .in_2(and_1_out), .in_3(or_1_out),
    .in_4(xor_1_out), .in_5(not_1_out), .in_6(deslocador_main_1_s), .in_7(deslocador_right_main_1_s), .out(G));
  // eh_zero eh_zero_1: pin names not known; wires that end beside it: G, zero
endmodule
